# Fritzing sketch GameSketch (saved by Fritzing 0.9.10b)
breadboards: 2

parts:
  Part1 = Adafruit Mini TFT Display - 0.96in 160x80 [part_number="Adafruit 3533"]
  Part2 = Thumb Joystick
  J1 = Piezo Speaker
  S1 = Pushbutton [package="[THT]"]
  S2 = Pushbutton [package="[THT]"]
  S3 = Pushbutton [package="[THT]"]
  S4 = Pushbutton [package="[THT]"]
  R1 = Resistor [tolerance=±5% resistance=220 package="2512 [SMD]"]
  Part3 = InvenSense MPU6050
  S5 = Pushbutton [package="[THT]"]
  R2 = Resistor [tolerance=±5% resistance=10k package="2512 [SMD]"]
  R3 = Resistor [tolerance=±5% resistance=1k package="2512 [SMD]"]
  R4 = Resistor [tolerance=±5% resistance=1k package="2512 [SMD]"]
  R5 = Resistor [tolerance=±5% resistance=1k package="2512 [SMD]"]
  R6 = Resistor [tolerance=±5% resistance=1k package="2512 [SMD]"]
  Part4 = Arduino Uno (Rev3)

nets:
  VCC: Part1.VIN, Part2.VCC, Part3.VCC, S5.Pin_1, S5.Pin_2, Part4.5V
  GND: Part1.GND, Part2.GND, S1.Pin_1, S1.Pin_2, S2.Pin_1, S2.Pin_2, S3.Pin_1, S3.Pin_2, S4.Pin_1, S4.Pin_2, R1.Pin_0, Part3.GND, R2.Pin_0, R6.Pin_0, Part4.GND
  N1: Part1.SCK, Part4.D13/SCK
  N2: Part1.MISO, Part4.D12/MISO
  N3: Part1.MOSI, Part4.D11_PWM/MOSI
  N4: Part1.TFTCS, Part4.D10_PWM/SS
  N5: Part1.DC, Part4.D8
  N6: Part1.SDCS, Part4.D4
  N7: Part2.SEL, Part4.D3_PWM
  N8: Part2.HORZ, Part4.A1
  N9: Part2.VERT, Part4.A0
  N10: J1.pin1, Part4.D7
  N11: J1.pin2, R1.Pin_1
  N12: S1.Pin_3, S1.Pin_4, R3.Pin_0, R4.Pin_0
  N13: S2.Pin_3, S2.Pin_4, R5.Pin_1, R6.Pin_1, Part4.A2
  N14: S3.Pin_3, S3.Pin_4, R4.Pin_1
  N15: S4.Pin_3, S4.Pin_4, R3.Pin_1, R5.Pin_0
  N16: Part3.SCL, Part4.A5/SCL
  N17: Part3.SDA, Part4.A4/SDA
  N18: Part3.INT, Part4.D2
  N19: S5.Pin_3, S5.Pin_4, R2.Pin_1, Part4.D5_PWM

custom parts:
  Adafruit Mini TFT Display - 0.96in 160x80: It's the size of your thumbnail, with glorious 160x80 pixel color... it's the Adafruit Mini TFT Breakout! This very very small display is only 0.96" diagonal, packed with RGB pixels, for making very small high-density displays. The display uses 4-wire SPI to communicate and has its own pixel-addressable frame buffer, it can be used with every kind of microcontroller. Even a very small one with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
